// Logisim project MARIE.circ as structural Verilog
module main (
  input  in_1,
  input  in_2,
  input  in_3,
  input  in_4,
  input  in_5,
  input  in_6
);

  wire _0_out, _1_2_out, _0001_out, _1_out, _2_out, _3_out, _4_out, _5_out, _6_out, _7_out, _8_out, _9_out,
       _0010_out, _0011_out, _0100_out, _0101_out, _0110_out, _0111_out, _1000_out, _1001_out, A_out,
       AC___0_2_out, AC___0_3_out, AC___0_out, AC_AC__MBR_out, AC_InReg_out, AC_MBR_out, ADD_2_out,
       ADD_3_out, ADD_out, and_1_out, B_out, button_1_out, C_out, Clear_2_out, Clear_out, clock_1_out,
       comparator_1_eq, comparator_1_gt, comparator_1_lt, comparator_2_eq, comparator_2_gt, comparator_2_lt,
       Cr_out, d_ff_1_q, d_ff_2_q, d_ff_2_qn, d_ff_3_q, d_ff_3_qn, d_ff_4_q, d_ff_4_qn, d_ff_5_q, d_ff_5_qn,
       d_ff_6_q, d_ff_6_qn, d_ff_7_q, d_ff_7_qn, d_ff_8_q, d_ff_8_qn, d_ff_9_q, d_ff_9_qn, d_ff_10_q,
       d_ff_10_qn, d_ff_11_q, d_ff_11_qn, D_out, demultiplexer_1_out0, demultiplexer_1_out1,
       demultiplexer_1_out2, demultiplexer_1_out3, demultiplexer_1_out4, demultiplexer_1_out5,
       demultiplexer_1_out6, demultiplexer_1_out7, E_out, Enter_out, F_out, HALT_out, INPUT_2_out, INPUT_out,
       JUMP_out, Lalt_out, LOAD_2_out, LOAD_3_out, LOAD_out, M_MAR__MBR_out, MAR_X_out, MBR_AC_out,
       MBR_M_MAR_out, multiplexer_1_out, Mw_out, nor_1_out, not_1_out, not_2_out, or_1_out, or_2_out,
       OUT_AC_out, OUTPUT_out, PC___PC___1_out, PC_X_out, SKIP_out, STORE_2_out, STORE_3_out, STORE_out,
       SUBT_2_out, SUBT_3_out, SUBT_out, toP1_out, Wait_out, xnor_1_out;
  wire [1:0] A0_out, IncrPC_out;
  wire [2:0] P0_out, P3_out;
  wire [3:0] MAR_q, MAR_q_2, MAR_q_3, multiplexer_2_out_2, multiplexer_3_out, One_out, ram_1_data,
       ram_1_data_2, ram_1_data_3, ram_1_data_4;
  wire [11:0] multiplexer_2_out, multiplexer_3_out_2, PC_q;
  wire [15:0] AC_q, adder_1_out, adder_2_out, InReg_q, IR_q, MBR_q, multiplexer_4_out, multiplexer_5_out,
       OutReg_q, shift_register_1_q0, subtractor_1_out;

  Button C (.out(C_out));
  Button D (.out(D_out));
  Button _9 (.out(_9_out));
  Button _8 (.out(_8_out));
  Button _4 (.out(_4_out));
  Button _5 (.out(_5_out));
  Button _1 (.out(_1_out));
  Button _0 (.out(_0_out));
  Button F (.out(F_out));
  Button E (.out(E_out));
  Button A (.out(A_out));
  Button B (.out(B_out));
  Button _7 (.out(_7_out));
  Button _6 (.out(_6_out));
  Button _3 (.out(_3_out));
  Button _2 (.out(_2_out));
  Button Clear (.out(Clear_out));
  Button Enter (.out(Enter_out));
  Hex_Digit_Display hex_digit_display_1 (.value(OutReg_q[15:12]));  // open: dp
  Hex_Digit_Display hex_digit_display_2 (.value(shift_register_1_q0[15:12]));  // open: dp
  Hex_Digit_Display hex_digit_display_3 (.value(OutReg_q[11:8]));  // open: dp
  Hex_Digit_Display hex_digit_display_4 (.value(OutReg_q[7:4]));  // open: dp
  Hex_Digit_Display hex_digit_display_5 (.value(shift_register_1_q0[11:8]));  // open: dp
  Hex_Digit_Display hex_digit_display_6 (.value(shift_register_1_q0[7:4]));  // open: dp
  or or_1 (or_1_out, A_out, B_out, C_out, _1_out, _2_out, _3_out, _4_out, _5_out, _6_out, _7_out, _8_out, _9_out, _0_out, D_out, E_out, F_out, Clear_out);
  Hex_Digit_Display hex_digit_display_7 (.value(OutReg_q[3:0]));  // open: dp
  Hex_Digit_Display hex_digit_display_8 (.value(shift_register_1_q0[3:0]));  // open: dp
  or One (One_out[0], F_out, B_out, _1_out, _5_out, _7_out, _3_out, _9_out, D_out);
  or Clear_2 (Clear_2_out, Clear_out, Enter_out);
  or Two (One_out[1], F_out, A_out, _7_out, _2_out, _6_out, _3_out, _7_out, B_out, E_out);
  or Four (One_out[2], F_out, E_out, _7_out, _4_out, _6_out, _5_out, C_out, D_out, F_out);
  or Eight (One_out[3], F_out, C_out, A_out, _8_out, E_out, _9_out, B_out, D_out);
  D_Flip_Flop d_ff_1 (.clk(clock_1_out), .D(Clear_2_out), .Q(d_ff_1_q));  // open: Qn, preset, en, reset
  Shift_Register #(.width(4), .length(4)) shift_register_1 (
    .in(One_out), .clk(or_1_out), .clr(d_ff_1_q), .q0(shift_register_1_q0[3:0]),
    .q1(shift_register_1_q0[7:4]), .q2(shift_register_1_q0[11:8]), .q3(shift_register_1_q0[15:12]));  // open: shift, out, load, d0, d1, d2, d3
  xnor xnor_1 (xnor_1_out, Wait_out, Enter_out);
  Multiplexer multiplexer_1 (.in0(in_1), .in1(1'b1), .out(multiplexer_1_out), .sel(xnor_1_out));  // open: en
  Button button_1 (.out(button_1_out));
  Demultiplexer #(.select(3)) demultiplexer_1 (
    .out0(demultiplexer_1_out0), .out1(demultiplexer_1_out1), .out2(demultiplexer_1_out2),
    .out3(demultiplexer_1_out3), .out4(demultiplexer_1_out4), .out5(demultiplexer_1_out5),
    .out6(demultiplexer_1_out6), .out7(demultiplexer_1_out7), .in(1'b1), .sel(P3_out));  // open: en
  or or_2 (or_2_out, Cr_out, in_2, button_1_out, d_ff_7_q);
  Hex_Digit_Display hex_digit_display_9 (.value(MAR_q_3));  // open: dp
  Clock clock_1 (.out(clock_1_out));
  Hex_Digit_Display hex_digit_display_10 (.value(MAR_q_2));  // open: dp
  Hex_Digit_Display hex_digit_display_11 (.value(MAR_q));  // open: dp
  not not_1 (not_1_out, demultiplexer_1_out0);
  LED led_1 (.in(clock_1_out));
  nor nor_1 (nor_1_out, d_ff_2_q, d_ff_3_q, d_ff_4_q, d_ff_5_q, d_ff_6_q, d_ff_7_q);
  D_Flip_Flop d_ff_2 (
    .clk(clock_1_out), .D(nor_1_out), .Q(d_ff_2_q), .Qn(d_ff_2_qn), .en(multiplexer_1_out), .reset(or_2_out));  // open: preset
  or toP1 (toP1_out, nor_1_out, d_ff_3_q);
  Register #(.width(12)) MAR (
    .D(multiplexer_2_out), .en(demultiplexer_1_out1), .Q({MAR_q_3, MAR_q_2, MAR_q}), .clk(clock_1_out));  // open: clr
  Register #(.width(12)) PC (
    .D(multiplexer_3_out_2), .en(demultiplexer_1_out2), .Q(PC_q), .clk(clock_1_out));  // open: clr
  Register #(.width(16)) MBR (
    .D({multiplexer_2_out_2, multiplexer_2_out}), .en(demultiplexer_1_out3), .Q(MBR_q), .clk(clock_1_out));  // open: clr
  Register #(.width(16)) AC (
    .D(multiplexer_5_out), .en(demultiplexer_1_out4), .Q(AC_q), .clk(clock_1_out));  // open: clr
  Register #(.width(16)) InReg (
    .D(shift_register_1_q0), .en(demultiplexer_1_out5), .Q(InReg_q), .clk(clock_1_out));  // open: clr
  Register #(.width(16)) OutReg (
    .D({multiplexer_2_out_2, multiplexer_2_out}), .en(demultiplexer_1_out6), .Q(OutReg_q), .clk(clock_1_out));  // open: clr
  Register #(.width(16)) IR (
    .D({multiplexer_2_out_2, multiplexer_2_out}), .en(demultiplexer_1_out7), .Q(IR_q), .clk(clock_1_out));  // open: clr
  D_Flip_Flop d_ff_3 (
    .clk(clock_1_out), .D(d_ff_2_q), .Q(d_ff_3_q), .Qn(d_ff_3_qn), .en(multiplexer_1_out), .reset(or_2_out));  // open: preset
  Hex_Digit_Display hex_digit_display_12 (.value(ram_1_data_4));  // open: dp
  D_Flip_Flop d_ff_4 (
    .clk(clock_1_out), .D(d_ff_3_q), .Q(d_ff_4_q), .Qn(d_ff_4_qn), .en(multiplexer_1_out), .reset(or_2_out));  // open: preset
  Hex_Digit_Display hex_digit_display_13 (.value(ram_1_data_2));  // open: dp
  Hex_Digit_Display hex_digit_display_14 (.value(ram_1_data_3));  // open: dp
  D_Flip_Flop d_ff_5 (
    .clk(clock_1_out), .D(d_ff_4_q), .Q(d_ff_5_q), .Qn(d_ff_5_qn), .en(multiplexer_1_out), .reset(or_2_out));  // open: preset
  Hex_Digit_Display hex_digit_display_15 (.value(ram_1_data));  // open: dp
  D_Flip_Flop d_ff_6 (
    .clk(clock_1_out), .D(d_ff_5_q), .Q(d_ff_6_q), .Qn(d_ff_6_qn), .en(multiplexer_1_out), .reset(or_2_out));  // open: preset
  RAM #(.addrWidth(12), .dataWidth(16), .bus("separate")) ram_1 (
    .addr({MAR_q_3, MAR_q_2, MAR_q}), .din({multiplexer_2_out_2, multiplexer_2_out}),
    .data({ram_1_data_4, ram_1_data_3, ram_1_data_2, ram_1_data}), .str(Mw_out), .clk(clock_1_out),
    .ld(not_1_out));  // open: sel, clr
  Adder #(.width(16)) adder_1 (.a({multiplexer_3_out, PC_q}), .b(16'h1), .out(adder_1_out));  // open: cin, cout
  D_Flip_Flop d_ff_7 (
    .clk(clock_1_out), .D(d_ff_6_q), .Q(d_ff_7_q), .Qn(d_ff_7_qn), .en(multiplexer_1_out), .reset(or_2_out));  // open: preset
  Multiplexer #(.select(3), .width(16)) multiplexer_2 (
    .in0({ram_1_data_4, ram_1_data_3, ram_1_data_2, ram_1_data}),
    .in1({multiplexer_2_out_2, MAR_q_3, MAR_q_2, MAR_q}), .in2({multiplexer_3_out, PC_q}), .in3(MBR_q),
    .in4(AC_q), .in5(InReg_q), .in6(IR_q), .out({multiplexer_2_out_2, multiplexer_2_out}), .sel(P0_out));  // open: in7, en
  Hex_Digit_Display hex_digit_display_16 (.value(multiplexer_2_out_2));  // open: dp
  Hex_Digit_Display hex_digit_display_17 (.value(multiplexer_2_out[11:8]));  // open: dp
  Multiplexer #(.select(2), .width(16)) multiplexer_3 (
    .in0({16{1'b0}}), .in1(adder_1_out), .in2({multiplexer_2_out_2, multiplexer_2_out}), .in3({16{1'b0}}),
    .out({multiplexer_3_out, multiplexer_3_out_2}), .sel(IncrPC_out));  // open: en
  and _1_2 (_1_2_out, IR_q[10], IR_q[11], comparator_1_eq);
  not not_2 (not_2_out, _1_2_out);
  Comparator #(.width(1)) comparator_1 (
    .a(IR_q[10]), .b(IR_q[11]), .gt(comparator_1_gt), .eq(comparator_1_eq), .lt(comparator_1_lt));
  Hex_Digit_Display hex_digit_display_18 (.value({in_3, P0_out}));  // open: dp
  Hex_Digit_Display hex_digit_display_19 (.value({in_4, P3_out}));  // open: dp
  Hex_Digit_Display hex_digit_display_20 (.value(multiplexer_2_out[3:0]));  // open: dp
  Hex_Digit_Display hex_digit_display_21 (.value(multiplexer_2_out[7:4]));  // open: dp
  Comparator #(.width(16)) comparator_2 (
    .a(AC_q), .b({16{1'b0}}), .gt(comparator_2_gt), .eq(comparator_2_eq), .lt(comparator_2_lt));
  LED led_2 (.in(P3_out[2]));
  Adder #(.width(16)) adder_2 (.a(AC_q), .b(MBR_q), .out(adder_2_out));  // open: cin, cout
  Subtractor #(.width(16)) subtractor_1 (.a(AC_q), .b(MBR_q), .out(subtractor_1_out));  // open: bin, bout
  and AC___0 (AC___0_out, comparator_2_lt, not_2_out);
  and AC___0_2 (AC___0_2_out, comparator_1_gt, comparator_2_gt);
  and AC___0_3 (AC___0_3_out, comparator_1_lt, comparator_2_eq);
  LED led_3 (.in(P0_out[1]));
  LED led_4 (.in(P0_out[2]));
  LED led_5 (.in(P3_out[0]));
  LED led_6 (.in(P3_out[1]));
  Hex_Digit_Display hex_digit_display_22 (.value({in_5, in_6, A0_out}));  // open: dp
  LED led_7 (.in(P0_out[0]));
  LED led_8 (.in(A0_out[0]));
  LED led_9 (.in(A0_out[1]));
  Multiplexer #(.select(2), .width(16)) multiplexer_4 (
    .in1(adder_2_out), .in2(subtractor_1_out), .out(multiplexer_4_out), .sel(A0_out));  // open: in0, in3, en
  Multiplexer #(.width(16)) multiplexer_5 (
    .in0({multiplexer_2_out_2, multiplexer_2_out}), .in1(multiplexer_4_out), .out(multiplexer_5_out),
    .sel(Lalt_out));  // open: en
  or PC___PC___1 (PC___PC___1_out, AC___0_out, AC___0_2_out, AC___0_3_out);
  and _0001 (_0001_out, d_ff_8_qn, d_ff_9_qn, d_ff_10_qn, d_ff_11_q);
  and LOAD (LOAD_out, _0001_out, d_ff_4_q);
  and LOAD_2 (LOAD_2_out, _0001_out, d_ff_5_q);
  or MBR_M_MAR (MBR_M_MAR_out, ADD_2_out, LOAD_2_out, SUBT_2_out);
  or P0 (P0_out[0], M_MAR__MBR_out, AC_MBR_out, AC_InReg_out);
  or P3 (P3_out[0], nor_1_out, d_ff_2_q, INPUT_out, MAR_X_out, MBR_M_MAR_out, MBR_AC_out);
  and LOAD_3 (LOAD_3_out, _0001_out, d_ff_6_q);
  buf AC_MBR (AC_MBR_out, LOAD_3_out);  // OR_Gate
  or P4 (P3_out[1], d_ff_2_q, IncrPC_out[0], MBR_M_MAR_out, OUT_AC_out, MBR_AC_out, PC_X_out);
  and STORE (STORE_out, _0010_out, d_ff_4_q);
  or MAR_X (MAR_X_out, SUBT_out, LOAD_out, STORE_out, ADD_out);
  and _0010 (_0010_out, d_ff_8_qn, d_ff_9_qn, d_ff_10_q, d_ff_11_qn);
  and STORE_2 (STORE_2_out, _0010_out, d_ff_5_q);
  and STORE_3 (STORE_3_out, _0010_out, d_ff_6_q);
  buf MBR_AC (MBR_AC_out, STORE_2_out);  // OR_Gate
  D_Flip_Flop d_ff_8 (.clk(clock_1_out), .D(IR_q[15]), .Q(d_ff_8_q), .Qn(d_ff_8_qn));  // open: preset, en, reset
  buf M_MAR__MBR (M_MAR__MBR_out, STORE_3_out);  // OR_Gate
  or P1 (P0_out[1], toP1_out, AC_MBR_out, PC_X_out, MAR_X_out, M_MAR__MBR_out);
  D_Flip_Flop d_ff_9 (.clk(clock_1_out), .D(IR_q[14]), .Q(d_ff_9_q), .Qn(d_ff_9_qn));  // open: preset, en, reset
  and _0011 (_0011_out, d_ff_8_qn, d_ff_9_qn, d_ff_10_q, d_ff_11_q);
  and ADD (ADD_out, d_ff_4_q, _0011_out);
  buf Mw (Mw_out, M_MAR__MBR_out);  // OR_Gate
  D_Flip_Flop d_ff_10 (.clk(clock_1_out), .D(IR_q[13]), .Q(d_ff_10_q), .Qn(d_ff_10_qn));  // open: preset, en, reset
  and ADD_2 (ADD_2_out, d_ff_5_q, _0011_out);
  and ADD_3 (ADD_3_out, d_ff_6_q, _0011_out);
  or AC_AC__MBR (AC_AC__MBR_out, SUBT_3_out, ADD_3_out);
  buf A0 (A0_out[0], ADD_3_out);  // OR_Gate
  buf A1 (A0_out[1], SUBT_3_out);  // OR_Gate
  D_Flip_Flop d_ff_11 (.clk(clock_1_out), .D(IR_q[12]), .Q(d_ff_11_q), .Qn(d_ff_11_qn));  // open: preset, en, reset
  and _0100 (_0100_out, d_ff_8_qn, d_ff_9_q, d_ff_10_qn, d_ff_11_qn);
  and SUBT (SUBT_out, _0100_out, d_ff_4_q);
  and SUBT_2 (SUBT_2_out, _0100_out, d_ff_5_q);
  and SUBT_3 (SUBT_3_out, _0100_out, d_ff_6_q);
  and _0101 (_0101_out, d_ff_8_qn, d_ff_9_q, d_ff_10_qn, d_ff_11_q);
  and INPUT (INPUT_out, _0101_out, d_ff_4_q);
  and INPUT_2 (INPUT_2_out, _0101_out, d_ff_5_q);
  or Wait (Wait_out, INPUT_out, HALT_out);
  buf AC_InReg (AC_InReg_out, INPUT_2_out);  // OR_Gate
  or P2 (P0_out[2], MBR_AC_out, MAR_X_out, AC_InReg_out, PC_X_out, OUT_AC_out);
  or P5 (P3_out[2], AC_MBR_out, d_ff_2_q, AC_AC__MBR_out, AC_InReg_out, INPUT_out, OUT_AC_out);
  and _0110 (_0110_out, d_ff_8_qn, d_ff_9_q, d_ff_10_q, d_ff_11_qn);
  and OUTPUT (OUTPUT_out, _0110_out, d_ff_4_q);
  buf OUT_AC (OUT_AC_out, OUTPUT_out);  // OR_Gate
  and _0111 (_0111_out, d_ff_8_qn, d_ff_9_q, d_ff_10_q, d_ff_11_q);
  and HALT (HALT_out, d_ff_4_q, _0111_out);
  and _1000 (_1000_out, d_ff_8_q, d_ff_9_qn, d_ff_10_qn, d_ff_11_qn);
  and SKIP (SKIP_out, d_ff_4_q, _1000_out, PC___PC___1_out);
  or IncrPC (IncrPC_out[0], d_ff_3_q, SKIP_out);
  buf PC_X (PC_X_out, JUMP_out);  // OR_Gate
  buf Cr (Cr_out, and_1_out);  // OR_Gate
  and _1001 (_1001_out, d_ff_8_q, d_ff_9_qn, d_ff_10_qn, d_ff_11_q);
  and JUMP (JUMP_out, d_ff_4_q, _1001_out);
  buf AltPC (IncrPC_out[1], JUMP_out);  // OR_Gate
  buf Lalt (Lalt_out, AC_AC__MBR_out);  // OR_Gate
  and and_1 (and_1_out, d_ff_8_qn, d_ff_9_qn, d_ff_4_q, d_ff_10_qn, d_ff_11_qn);

  // Notes on the sheet:
  //   INPUT
  //   OutReg
  //   InReg
  //   Clock
  //   Address
  //   MAR 0-11
  //   PC 0-11 
  //   MAR 12-15
  //   PC 12-15
  //   T1
  //   T4
  //   T3
  //   T2
  //   T0
  //   T6
  //   T5
  //   Data
  //   Bus
  //   Read Address
  //   Write Address
  //   AC
  //   MBR
  //   P1
  //   P2
  //   P0
  //   T3
  //   P3
  //   P4
  //   P5
  //   A0
  //   A1
  //   Cr
  //   Mw
  //   Lalt
  //   IncrPC
  //   AltPC
  //   T4
  //   T5
  //   LOAD
  //   STORE
  //   Instruction
  //   ADD
  //   SUBT
  //   INPUT
  //   Output
  //   HALT
  //   SKIP
  //   JUMP
  //   T5
  //   T4
  //   T3
endmodule
